// Logisim project LATEST ENCODER THING.circ as structural Verilog: 1 circuit, main circuit main
module main (
  input  s0,
  input  s1,
  input  s2,
  input  s3,
  input  s4,
  input  s5,
  input  s6,
  input  s7,
  input  in_9,
  input  in_10,
  input  in_11,
  input  in_12,
  input  in_13,
  input  in_14,
  input  in_15
);

  wire and_1_out, and_2_out, and_3_out, and_4_out, and_5_out, and_6_out, and_8_out, and_9_out, and_10_out,
       and_11_out, and_12_out, and_13_out, and_14_out, and_15_out, and_16_out, and_17_out, not_1_out,
       not_2_out, not_3_out, not_4_out, not_5_out, not_6_out, or_1_out, or_2_out, or_3_out, or_4_out,
       or_5_out, or_6_out, or_7_out, or_8_out, or_9_out, or_10_out, or_11_out, or_12_out, or_13_out,
       or_14_out, or_15_out, or_16_out, or_17_out, or_18_out, or_19_out, or_20_out, undriven;

  or or_1 (or_1_out, s1, s3, s5, s7);
  or or_2 (or_2_out, s2, s3, s6, s7);
  or or_3 (or_3_out, s4, s5, s6, s7);
  not not_1 (not_1_out, or_1_out);
  not not_2 (not_2_out, or_2_out);
  not not_3 (not_3_out, or_3_out);
  and and_1 (and_1_out, not_3_out, or_1_out);
  and and_2 (and_2_out, not_3_out, not_1_out);
  and and_3 (and_3_out, or_1_out, or_2_out);
  and and_4 (and_4_out, not_2_out, not_1_out);
  and and_5 (and_5_out, not_3_out, not_2_out);
  and and_6 (and_6_out, not_3_out, or_2_out);
  and and_7 (and_6_out, not_3_out, not_1_out);
  and and_8 (and_8_out, or_2_out, not_1_out);
  and and_9 (and_9_out, not_3_out, not_2_out, or_1_out);
  or or_4 (or_4_out, and_1_out, and_6_out, or_2_out, s0);
  or or_5 (or_5_out, and_2_out, and_4_out, and_5_out, s0);
  or or_6 (or_6_out, and_3_out, and_4_out, not_3_out, or_2_out);
  or or_7 (or_7_out, and_5_out, undriven, and_8_out, s0);
  or or_8 (or_8_out, and_6_out, and_8_out);
  or or_9 (or_9_out, or_1_out, not_2_out, not_3_out, s0);
  or or_10 (or_10_out, undriven, and_6_out, and_8_out, and_9_out, s0);
  or or_11 (or_11_out, in_9, in_11, in_13, in_15);
  or or_12 (or_12_out, in_10, in_11, in_14, in_15);
  or or_13 (or_13_out, in_12, in_14, in_13, in_15);
  _7_Segment_Display u_7_segment_display_1 (
    .g(or_6_out), .f(or_5_out), .a(or_4_out), .b(or_10_out), .e(or_7_out), .d(or_8_out), .c(or_9_out), .dp(s0));
  not not_4 (not_4_out, or_11_out);
  not not_5 (not_5_out, or_12_out);
  not not_6 (not_6_out, or_13_out);
  and and_10 (and_10_out, not_4_out, not_5_out, not_6_out);
  and and_11 (and_11_out, or_11_out, not_5_out, not_6_out);
  and and_12 (and_12_out, not_6_out, or_12_out, not_4_out);
  and and_13 (and_13_out, or_11_out, or_12_out, not_6_out);
  and and_14 (and_14_out, or_13_out, not_5_out, not_4_out);
  and and_15 (and_15_out, or_11_out, not_5_out, or_13_out);
  and and_16 (and_16_out, or_13_out, or_12_out, not_4_out);
  and and_17 (and_17_out, or_11_out, or_12_out, or_13_out);
  or or_14 (or_14_out, and_11_out, and_12_out, and_13_out, and_14_out, and_17_out);
  or or_15 (or_15_out, and_12_out, and_13_out, and_15_out, and_16_out, and_17_out);
  or or_16 (or_16_out, and_14_out, and_15_out, and_16_out);
  or or_17 (or_17_out, and_12_out, and_13_out, and_14_out, and_16_out, and_15_out);
  or or_18 (or_18_out, and_12_out, and_16_out);
  or or_19 (or_19_out, and_12_out, and_13_out, and_15_out, and_16_out);
  or or_20 (or_20_out, and_11_out, and_13_out, and_14_out, and_15_out, and_16_out, and_17_out);
  _7_Segment_Display u_7_segment_display_2 (
    .g(or_17_out), .f(or_16_out), .a(or_15_out), .b(or_14_out), .e(or_18_out), .d(or_19_out), .c(or_20_out),
    .dp(and_10_out));

  // Notes on the sheet:
  //   0000001
  //   0000010
  //   0000100
  //   0001000
  //   0010000
  //   0100000
  //   1000000
  //   001
  //   010
  //   011
  //   100
  //   101
  //   110
  //   111
endmodule
