// Logisim project prob1_1a.circ as structural Verilog: 1 circuit, main circuit main
module main (
  input  a,
  input  b,
  input  c,
  output F
);

  wire and_1_out, and_2_out, or_1_out, or_2_out, or_3_out;

  or or_1 (or_1_out, c, b);
  and and_1 (and_1_out, b, c);
  and and_2 (and_2_out, b, a);
  or or_2 (or_2_out, or_1_out, a);
  or or_3 (or_3_out, and_1_out, and_2_out);
  or or_4 (F, or_2_out, or_3_out);
endmodule
