// Logisim project prob1_1b.circ as structural Verilog: 1 circuit, main circuit main
module main (
  input  a,
  input  b,
  input  c,
  output G
);

  wire and_1_out, and_2_out, and_3_out, and_4_out, and_5_out, and_6_out, controlled_inverter_1_out,
       nor_1_out, or_1_out;

  and and_1 (and_1_out, a, a);
  and and_2 (and_2_out, a, c);
  Controlled_Inverter controlled_inverter_1 (.in(b), .out(controlled_inverter_1_out));  // open: en
  nor nor_1 (nor_1_out, a, b);
  and and_3 (and_3_out, and_1_out, c);
  and and_4 (and_4_out, and_2_out, controlled_inverter_1_out);
  and and_5 (and_5_out, and_4_out, c);
  and and_6 (and_6_out, nor_1_out, c);
  or or_1 (or_1_out, and_3_out, and_5_out);
  or or_2 (G, or_1_out, and_6_out);
endmodule
