// Logisim project problem2.circ as structural Verilog: 1 circuit, main circuit main
module main (
);

  wire and_1_out, and_2_out, and_3_out, and_4_out, button_1_out, nor_1_out, nor_2_out, nor_4_out, not_1_out,
       not_2_out, not_3_out;

  Button button_1 (.out(button_1_out));
  not not_1 (not_1_out, button_1_out);
  not not_2 (not_2_out, button_1_out);
  and and_1 (and_1_out, button_1_out, not_1_out);
  and and_2 (and_2_out, not_1_out, not_2_out);
  nor nor_1 (nor_1_out, and_1_out, nor_2_out);
  nor nor_2 (nor_2_out, nor_1_out, and_2_out);
  and and_3 (and_3_out, nor_2_out, button_1_out);
  and and_4 (and_4_out, button_1_out, not_3_out);
  not not_3 (not_3_out, nor_2_out);
  nor nor_3 (button_1_out, and_3_out, nor_4_out);
  nor nor_4 (nor_4_out, button_1_out, and_4_out);
  LED led_1 (.in(nor_4_out));

  // Notes on the sheet:
  //   741G04
  //   741G04
  //   741G04
  //   Pin: SOT753
  //   741G08
  //   Pin: SOT753
  //   741G08
  //   Pin: SOT753
  //   741G02
  //   741G02
  //   Pin: SOT753
  //   Pin: SOT753
  //   741G08
  //   741G04
  //   741G08
  //   Pin: SOT753
  //   Pin: SOT753
  //   741G02
  //   741G02
  //   Pin: SOT753
endmodule
