// Logisim project problem3num1.circ as structural Verilog: 1 circuit, main circuit main
module main (
  input  in_1,
  input  in_2,
  input  in_3,
  input  in_4,
  output A_C,
  output D0,
  output D1,
  output D2,
  output D3,
  output Engine_Starter,
  output Wipers
);

  wire and_1_out, and_2_out, and_3_out, and_4_out, and_5_out, nor_1_out, nor_2_out, not_1_out, not_2_out,
       not_3_out, not_4_out;

  nor nor_1 (nor_1_out, in_1, in_2);
  not not_1 (not_1_out, in_3);
  not not_2 (not_2_out, in_3);
  nor nor_2 (nor_2_out, in_3, in_4);
  not not_3 (not_3_out, in_4);
  and and_1 (and_1_out, not_2_out, in_4);
  not not_4 (not_4_out, nor_1_out);
  and and_2 (and_2_out, not_4_out, in_2);
  and and_3 (and_3_out, in_4, not_1_out);
  and and_4 (and_4_out, in_3, not_3_out);
  and and_5 (and_5_out, in_3, in_4);
  and and_6 (A_C, nor_1_out, nor_2_out);
  and and_7 (D0, nor_1_out, and_3_out);
  and and_8 (D1, nor_1_out, and_4_out);
  and and_9 (D2, nor_1_out, and_5_out);
  and and_10 (D3, and_2_out, nor_2_out);
  and and_11 (Engine_Starter, and_2_out, and_1_out);
  and and_12 (Wipers, and_2_out, and_5_out);

  // Notes on the sheet:
  //   1001 Devices Off
  //   0000 A/C On
  //   0001 D0
  //   0010 D1 Locked
  //   0011 D2 Locked
  //   0100 D3 Locked
  //   0111 Wipers
  //   0101 Engine Started
endmodule
