// Logisim project problem1.circ as structural Verilog: 1 circuit, main circuit main
module main (
  input  in_1,
  input  in_2,
  input  in_3,
  input  in_4,
  input  in_5,
  input  in_6,
  output out_7
);

  wire and_1_out, and_2_out, clock_1_out, clock_2_out, d_ff_1_q, d_ff_2_q, d_ff_3_q, d_ff_4_q, d_ff_5_q,
       d_ff_6_q, d_ff_7_q, d_ff_8_q, d_ff_9_q, d_ff_10_q, d_ff_11_q, d_ff_12_q, d_ff_13_q, d_ff_14_q,
       d_ff_15_q, d_ff_16_q, d_ff_17_q, d_ff_18_q, d_ff_19_q, d_ff_20_q, d_ff_21_q, d_ff_22_q, d_ff_23_q,
       multiplexer_1_out, multiplexer_2_out, multiplexer_3_out, not_1_out, undriven, undriven_2, undriven_3;

  Clock #(.lowDuration(20)) clock_1 (.out(clock_1_out));
  and and_1 (and_1_out, in_1, in_2);
  not not_1 (not_1_out, in_1);
  and and_2 (and_2_out, not_1_out, in_3);
  D_Flip_Flop d_ff_1 (.clk(clock_1_out), .D(in_4), .Q(d_ff_1_q), .en(undriven));  // open: Qn, preset, reset
  LED led_1 (.in(d_ff_1_q));
  or or_1 (out_7, and_1_out, and_2_out);
  D_Flip_Flop d_ff_2 (.clk(clock_1_out), .D(d_ff_1_q), .Q(d_ff_2_q), .en(undriven_2));  // open: Qn, preset, reset
  LED led_2 (.in(d_ff_2_q));
  Clock #(.lowDuration(20)) clock_2 (.out(clock_2_out));
  D_Flip_Flop d_ff_3 (.clk(clock_1_out), .D(d_ff_4_q), .Q(d_ff_3_q));  // open: Qn, preset, en, reset
  D_Flip_Flop d_ff_4 (.clk(clock_1_out), .D(d_ff_2_q), .Q(d_ff_4_q), .en(undriven_3));  // open: Qn, preset, reset
  LED led_3 (.in(d_ff_4_q));
  D_Flip_Flop d_ff_5 (.clk(clock_1_out), .D(d_ff_3_q), .Q(d_ff_5_q));  // open: Qn, preset, en, reset
  LED led_4 (.in(d_ff_3_q));
  LED led_5 (.in(d_ff_5_q));
  Multiplexer multiplexer_1 (.in0(d_ff_8_q), .in1(in_5), .out(multiplexer_1_out), .sel(in_6));  // open: en
  D_Flip_Flop d_ff_6 (.clk(clock_2_out), .D(multiplexer_1_out), .Q(d_ff_6_q));  // open: Qn, preset, en, reset
  LED led_6 (.in(d_ff_6_q));
  D_Flip_Flop d_ff_7 (.clk(clock_1_out), .D(d_ff_5_q), .Q(d_ff_7_q));  // open: Qn, preset, en, reset
  LED led_7 (.in(d_ff_7_q));
  Multiplexer multiplexer_2 (.in0(d_ff_10_q), .in1(d_ff_6_q), .out(multiplexer_2_out), .sel(in_6));  // open: en
  D_Flip_Flop d_ff_8 (.clk(clock_2_out), .D(multiplexer_2_out), .Q(d_ff_8_q));  // open: Qn, preset, en, reset
  LED led_8 (.in(d_ff_8_q));
  D_Flip_Flop d_ff_9 (.clk(clock_1_out), .D(d_ff_7_q), .Q(d_ff_9_q));  // open: Qn, preset, en, reset
  LED led_9 (.in(d_ff_9_q));
  Multiplexer multiplexer_3 (.in0(d_ff_10_q), .in1(d_ff_8_q), .out(multiplexer_3_out), .sel(in_6));  // open: en
  D_Flip_Flop d_ff_10 (.clk(clock_2_out), .D(multiplexer_3_out), .Q(d_ff_10_q));  // open: Qn, preset, en, reset
  D_Flip_Flop d_ff_11 (.clk(clock_1_out), .D(d_ff_9_q), .Q(d_ff_11_q));  // open: Qn, preset, en, reset
  LED led_10 (.in(d_ff_11_q));
  LED led_11 (.in(d_ff_10_q));
  D_Flip_Flop d_ff_12 (.clk(clock_1_out), .D(d_ff_11_q), .Q(d_ff_12_q));  // open: Qn, preset, en, reset
  LED led_12 (.in(d_ff_12_q));
  D_Flip_Flop d_ff_13 (.clk(clock_1_out), .D(d_ff_12_q), .Q(d_ff_13_q));  // open: Qn, preset, en, reset
  LED led_13 (.in(d_ff_13_q));
  D_Flip_Flop d_ff_14 (.clk(clock_1_out), .D(d_ff_15_q), .Q(d_ff_14_q));  // open: Qn, preset, en, reset
  D_Flip_Flop d_ff_15 (.clk(clock_1_out), .D(d_ff_13_q), .Q(d_ff_15_q));  // open: Qn, preset, en, reset
  LED led_14 (.in(d_ff_15_q));
  D_Flip_Flop d_ff_16 (.clk(clock_1_out), .D(d_ff_14_q), .Q(d_ff_16_q));  // open: Qn, preset, en, reset
  LED led_15 (.in(d_ff_16_q));
  LED led_16 (.in(d_ff_14_q));
  D_Flip_Flop d_ff_17 (.clk(clock_1_out), .D(d_ff_16_q), .Q(d_ff_17_q));  // open: Qn, preset, en, reset
  LED led_17 (.in(d_ff_17_q));
  D_Flip_Flop d_ff_18 (.clk(clock_1_out), .D(d_ff_17_q), .Q(d_ff_18_q));  // open: Qn, preset, en, reset
  LED led_18 (.in(d_ff_18_q));
  D_Flip_Flop d_ff_19 (.clk(clock_1_out), .D(d_ff_18_q), .Q(d_ff_19_q));  // open: Qn, preset, en, reset
  LED led_19 (.in(d_ff_19_q));
  D_Flip_Flop d_ff_20 (.clk(clock_1_out), .D(d_ff_19_q), .Q(d_ff_20_q));  // open: Qn, preset, en, reset
  LED led_20 (.in(d_ff_20_q));
  D_Flip_Flop d_ff_21 (.clk(clock_1_out), .D(d_ff_20_q), .Q(d_ff_21_q));  // open: Qn, preset, en, reset
  LED led_21 (.in(d_ff_21_q));
  D_Flip_Flop d_ff_22 (.clk(clock_1_out), .D(d_ff_23_q), .Q(d_ff_22_q));  // open: Qn, preset, en, reset
  D_Flip_Flop d_ff_23 (.clk(clock_1_out), .D(d_ff_21_q), .Q(d_ff_23_q));  // open: Qn, preset, en, reset
  LED led_22 (.in(d_ff_23_q));
  LED led_23 (.in(d_ff_22_q));
endmodule
